// Logisim project cpu.circ as structural Verilog
module main (
  input  I0,
  input  I1,
  input  I2,
  input  I3,
  input  RESET,
  output O0,
  output O1,
  output O2,
  output O3
);

  wire and_1_out, and_2_out, and_3_out, and_4_out, clock_1_out, count_4_1_q0, count_4_1_q1, count_4_1_q2,
       count_4_1_q3, d_ff_1_q, fa_4_1_co, fa_4_1_s0, fa_4_1_s1, fa_4_1_s2, fa_4_1_s3, ins_decoder_1_im0,
       ins_decoder_1_im1, ins_decoder_1_im2, ins_decoder_1_im3, ins_decoder_1_l_a, ins_decoder_1_l_b,
       ins_decoder_1_l_c, ins_decoder_1_l_d, ins_decoder_1_s0, ins_decoder_1_s1, multiplexer_4_2_1__0y,
       multiplexer_4_2_1__1y, multiplexer_4_2_2__0y, multiplexer_4_2_2__1y, not_1_out, reg_4_1_q0,
       reg_4_1_q1, reg_4_1_q2, reg_4_1_q3, reg_4_2_q0, reg_4_2_q1, reg_4_2_q2, reg_4_2_q3, rom_timer_1_d0,
       rom_timer_1_d1, rom_timer_1_d2, rom_timer_1_d3, rom_timer_1_d4, rom_timer_1_d5, rom_timer_1_d6,
       rom_timer_1_d7;

  and and_1 (and_1_out, ins_decoder_1_l_b, not_1_out);
  and and_2 (and_2_out, ins_decoder_1_l_a, not_1_out);
  and and_3 (and_3_out, ins_decoder_1_l_d, not_1_out);
  and and_4 (and_4_out, ins_decoder_1_l_c, not_1_out);
  Clock clock_1 (.out(clock_1_out));
  reg_4 reg_4_1 (
    .D0(fa_4_1_s0), .D1(fa_4_1_s1), .D2(fa_4_1_s2), .D3(fa_4_1_s3), .Q0(reg_4_1_q0), .Q1(reg_4_1_q1),
    .Q2(reg_4_1_q2), .Q3(reg_4_1_q3), .L(and_2_out), .CK(clock_1_out), .R0(RESET));  // open: R1
  reg_4 reg_4_2 (
    .D0(fa_4_1_s0), .D1(fa_4_1_s1), .D2(fa_4_1_s2), .D3(fa_4_1_s3), .Q0(reg_4_2_q0), .Q1(reg_4_2_q1),
    .Q2(reg_4_2_q2), .Q3(reg_4_2_q3), .L(and_1_out), .CK(clock_1_out), .R0(RESET));  // open: R1
  reg_4 reg_4_3 (
    .D0(fa_4_1_s0), .D1(fa_4_1_s1), .D2(fa_4_1_s2), .D3(fa_4_1_s3), .Q0(O0), .Q1(O1), .Q2(O2), .Q3(O3),
    .L(and_4_out), .CK(clock_1_out), .R0(RESET));  // open: R1
  count_4 count_4_1 (
    .D0(fa_4_1_s0), .D1(fa_4_1_s1), .D2(fa_4_1_s2), .D3(fa_4_1_s3), .L(and_3_out), .CK(clock_1_out),
    .RST(RESET), .Q3(count_4_1_q3), .Q2(count_4_1_q2), .Q1(count_4_1_q1), .Q0(count_4_1_q0));
  not not_1 (not_1_out, RESET);
  LED led_1 (.in(reg_4_1_q3));
  LED led_2 (.in(reg_4_1_q1));
  LED led_3 (.in(reg_4_1_q2));
  LED led_4 (.in(reg_4_2_q3));
  LED led_5 (.in(reg_4_2_q2));
  LED led_6 (.in(reg_4_2_q1));
  LED led_7 (.in(O2));
  LED led_8 (.in(O3));
  LED led_9 (.in(O1));
  LED led_10 (.in(count_4_1_q3));
  LED led_11 (.in(count_4_1_q2));
  LED led_12 (.in(count_4_1_q1));
  LED led_13 (.in(reg_4_1_q0));
  LED led_14 (.in(reg_4_2_q0));
  LED led_15 (.in(O0));
  rom_Timer rom_timer_1 (
    .A0(count_4_1_q0), .A1(count_4_1_q1), .A2(count_4_1_q2), .A3(count_4_1_q3), .D0(rom_timer_1_d0),
    .D1(rom_timer_1_d1), .D2(rom_timer_1_d2), .D3(rom_timer_1_d3), .D4(rom_timer_1_d4), .D5(rom_timer_1_d5),
    .D6(rom_timer_1_d6), .D7(rom_timer_1_d7));
  LED led_16 (.in(count_4_1_q0));
  ins_decoder ins_decoder_1 (
    .D0(rom_timer_1_d0), .D1(rom_timer_1_d1), .D2(rom_timer_1_d2), .D3(rom_timer_1_d3), .D4(rom_timer_1_d4),
    .D5(rom_timer_1_d5), .D6(rom_timer_1_d6), .D7(rom_timer_1_d7), .C(d_ff_1_q), .L_A(ins_decoder_1_l_a),
    .L_B(ins_decoder_1_l_b), .L_C(ins_decoder_1_l_c), .L_D(ins_decoder_1_l_d), .S0(ins_decoder_1_s0),
    .S1(ins_decoder_1_s1), .im0(ins_decoder_1_im0), .im1(ins_decoder_1_im1), .im2(ins_decoder_1_im2),
    .im3(ins_decoder_1_im3));
  multiplexer_4_2 multiplexer_4_2_1 (
    ._0A0(reg_4_1_q0), ._0A1(reg_4_2_q0), ._0A2(I0), ._0A3(1'b0), .S1(ins_decoder_1_s1),
    .S0(ins_decoder_1_s0), ._0Y(multiplexer_4_2_1__0y), ._1Y(multiplexer_4_2_1__1y), ._1A0(reg_4_1_q1),
    ._1A1(reg_4_2_q1), ._1A2(I1), ._1A3(1'b0));
  multiplexer_4_2 multiplexer_4_2_2 (
    ._0A0(reg_4_1_q2), ._0A1(reg_4_2_q2), ._0A2(I2), ._0A3(1'b0), .S1(ins_decoder_1_s1),
    .S0(ins_decoder_1_s0), ._0Y(multiplexer_4_2_2__0y), ._1Y(multiplexer_4_2_2__1y), ._1A0(reg_4_1_q3),
    ._1A1(reg_4_2_q3), ._1A2(I3), ._1A3(1'b0));
  rom_LED rom_led_1 ();  // open: A0, A1, A2, A3, D0, D1, D2, D3, D4, D5, D6, D7
  FA_4 fa_4_1 (
    .Ci(1'b0), .A0(multiplexer_4_2_1__0y), .B0(ins_decoder_1_im0), .A1(multiplexer_4_2_1__1y),
    .B1(ins_decoder_1_im1), .A2(multiplexer_4_2_2__0y), .B2(ins_decoder_1_im2), .A3(multiplexer_4_2_2__1y),
    .B3(ins_decoder_1_im3), .S0(fa_4_1_s0), .S1(fa_4_1_s1), .S2(fa_4_1_s2), .S3(fa_4_1_s3), .Co(fa_4_1_co));
  LED led_17 (.in(d_ff_1_q));
  D_Flip_Flop d_ff_1 (.clk(clock_1_out), .D(fa_4_1_co), .Q(d_ff_1_q));  // open: Qn, preset, en, reset

  // Notes on the sheet:
  //   LOAD
  //   CLOCK
  //   REG[A]
  //   REG[B]
  //   REG[C]
  //   REG[D]
  //   IO_OUT
  //   IO_IN
  //   BYPASS
  //   SELECTOR
  //   immediate
  //   ALU
  //   carry flag
endmodule

module rom_LED (
  input  A0,
  input  A1,
  input  A2,
  input  A3,
  output D0,
  output D1,
  output D2,
  output D3,
  output D4,
  output D5,
  output D6,
  output D7
);

  wire line_decoder_4_to16_1_o0, line_decoder_4_to16_1_o1, line_decoder_4_to16_1_o2,
       line_decoder_4_to16_1_o3, line_decoder_4_to16_1_o4, line_decoder_4_to16_1_o5,
       line_decoder_4_to16_1_o6, line_decoder_4_to16_1_o7, line_decoder_4_to16_1_o8,
       line_decoder_4_to16_1_o9, line_decoder_4_to16_1_o10, line_decoder_4_to16_1_o11,
       line_decoder_4_to16_1_o12, line_decoder_4_to16_1_o13, line_decoder_4_to16_1_o14,
       line_decoder_4_to16_1_o15, rom_1byte_1_d0_2, rom_1byte_1_d1_2, rom_1byte_1_d2_2, rom_1byte_1_d3_2,
       rom_1byte_1_d4_2, rom_1byte_1_d5_2, rom_1byte_1_d6_2, rom_1byte_1_d7_2, rom_1byte_2_d0_2,
       rom_1byte_2_d1_2, rom_1byte_2_d2_2, rom_1byte_2_d3_2, rom_1byte_2_d4_2, rom_1byte_2_d5_2,
       rom_1byte_2_d6_2, rom_1byte_2_d7_2, rom_1byte_3_d0_2, rom_1byte_3_d1_2, rom_1byte_3_d2_2,
       rom_1byte_3_d3_2, rom_1byte_3_d4_2, rom_1byte_3_d5_2, rom_1byte_3_d6_2, rom_1byte_3_d7_2,
       rom_1byte_4_d0_2, rom_1byte_4_d1_2, rom_1byte_4_d2_2, rom_1byte_4_d3_2, rom_1byte_4_d4_2,
       rom_1byte_4_d5_2, rom_1byte_4_d6_2, rom_1byte_4_d7_2, rom_1byte_5_d0_2, rom_1byte_5_d1_2,
       rom_1byte_5_d2_2, rom_1byte_5_d3_2, rom_1byte_5_d4_2, rom_1byte_5_d5_2, rom_1byte_5_d6_2,
       rom_1byte_5_d7_2, rom_1byte_6_d0_2, rom_1byte_6_d1_2, rom_1byte_6_d2_2, rom_1byte_6_d3_2,
       rom_1byte_6_d4_2, rom_1byte_6_d5_2, rom_1byte_6_d6_2, rom_1byte_6_d7_2, rom_1byte_7_d0_2,
       rom_1byte_7_d1_2, rom_1byte_7_d2_2, rom_1byte_7_d3_2, rom_1byte_7_d4_2, rom_1byte_7_d5_2,
       rom_1byte_7_d6_2, rom_1byte_7_d7_2, rom_1byte_8_d0_2, rom_1byte_8_d1_2, rom_1byte_8_d2_2,
       rom_1byte_8_d3_2, rom_1byte_8_d4_2, rom_1byte_8_d5_2, rom_1byte_8_d6_2, rom_1byte_8_d7_2,
       rom_1byte_9_d0_2, rom_1byte_9_d1_2, rom_1byte_9_d2_2, rom_1byte_9_d3_2, rom_1byte_9_d4_2,
       rom_1byte_9_d5_2, rom_1byte_9_d6_2, rom_1byte_9_d7_2, rom_1byte_10_d0_2, rom_1byte_10_d1_2,
       rom_1byte_10_d2_2, rom_1byte_10_d3_2, rom_1byte_10_d4_2, rom_1byte_10_d5_2, rom_1byte_10_d6_2,
       rom_1byte_10_d7_2, rom_1byte_11_d0_2, rom_1byte_11_d1_2, rom_1byte_11_d2_2, rom_1byte_11_d3_2,
       rom_1byte_11_d4_2, rom_1byte_11_d5_2, rom_1byte_11_d6_2, rom_1byte_11_d7_2, rom_1byte_12_d0_2,
       rom_1byte_12_d1_2, rom_1byte_12_d2_2, rom_1byte_12_d3_2, rom_1byte_12_d4_2, rom_1byte_12_d5_2,
       rom_1byte_12_d6_2, rom_1byte_12_d7_2, rom_1byte_13_d0_2, rom_1byte_13_d1_2, rom_1byte_13_d2_2,
       rom_1byte_13_d3_2, rom_1byte_13_d4_2, rom_1byte_13_d5_2, rom_1byte_13_d6_2, rom_1byte_13_d7_2,
       rom_1byte_14_d0_2, rom_1byte_14_d1_2, rom_1byte_14_d2_2, rom_1byte_14_d3_2, rom_1byte_14_d4_2,
       rom_1byte_14_d5_2, rom_1byte_14_d6_2, rom_1byte_14_d7_2, rom_1byte_15_d0_2, rom_1byte_15_d1_2,
       rom_1byte_15_d2_2, rom_1byte_15_d3_2, rom_1byte_15_d4_2, rom_1byte_15_d5_2, rom_1byte_15_d6_2,
       rom_1byte_15_d7_2, rom_1byte_16_d0_2, rom_1byte_16_d1_2, rom_1byte_16_d2_2, rom_1byte_16_d3_2,
       rom_1byte_16_d4_2, rom_1byte_16_d5_2, rom_1byte_16_d6_2, rom_1byte_16_d7_2;

  line_decoder_4_to16 line_decoder_4_to16_1 (
    .S0(A0), .S1(A1), .S3(A2), .S4(A3), .In(1'b1), .O15(line_decoder_4_to16_1_o15),
    .O14(line_decoder_4_to16_1_o14), .O13(line_decoder_4_to16_1_o13), .O12(line_decoder_4_to16_1_o12),
    .O11(line_decoder_4_to16_1_o11), .O10(line_decoder_4_to16_1_o10), .O9(line_decoder_4_to16_1_o9),
    .O8(line_decoder_4_to16_1_o8), .O7(line_decoder_4_to16_1_o7), .O6(line_decoder_4_to16_1_o6),
    .O5(line_decoder_4_to16_1_o5), .O4(line_decoder_4_to16_1_o4), .O3(line_decoder_4_to16_1_o3),
    .O2(line_decoder_4_to16_1_o2), .O1(line_decoder_4_to16_1_o1), .O0(line_decoder_4_to16_1_o0));
  rom_1byte rom_1byte_1 (
    .E(line_decoder_4_to16_1_o0), .D0_2(rom_1byte_1_d0_2), .D1_2(rom_1byte_1_d1_2), .D2_2(rom_1byte_1_d2_2),
    .D3_2(rom_1byte_1_d3_2), .D4_2(rom_1byte_1_d4_2), .D5_2(rom_1byte_1_d5_2), .D6_2(rom_1byte_1_d6_2),
    .D7_2(rom_1byte_1_d7_2), .D0(1'b1), .D1(1'b1), .D2(1'b0), .D3(1'b0), .D4(1'b1), .D5(1'b1), .D6(1'b0),
    .D7(1'b1));
  rom_1byte rom_1byte_2 (
    .E(line_decoder_4_to16_1_o1), .D0_2(rom_1byte_2_d0_2), .D1_2(rom_1byte_2_d1_2), .D2_2(rom_1byte_2_d2_2),
    .D3_2(rom_1byte_2_d3_2), .D4_2(rom_1byte_2_d4_2), .D5_2(rom_1byte_2_d5_2), .D6_2(rom_1byte_2_d6_2),
    .D7_2(rom_1byte_2_d7_2), .D0(1'b0), .D1(1'b1), .D2(1'b1), .D3(1'b0), .D4(1'b1), .D5(1'b1), .D6(1'b0),
    .D7(1'b1));
  rom_1byte rom_1byte_3 (
    .E(line_decoder_4_to16_1_o2), .D0_2(rom_1byte_3_d0_2), .D1_2(rom_1byte_3_d1_2), .D2_2(rom_1byte_3_d2_2),
    .D3_2(rom_1byte_3_d3_2), .D4_2(rom_1byte_3_d4_2), .D5_2(rom_1byte_3_d5_2), .D6_2(rom_1byte_3_d6_2),
    .D7_2(rom_1byte_3_d7_2), .D0(1'b0), .D1(1'b0), .D2(1'b1), .D3(1'b1), .D4(1'b1), .D5(1'b1), .D6(1'b0),
    .D7(1'b1));
  rom_1byte rom_1byte_4 (
    .E(line_decoder_4_to16_1_o3), .D0_2(rom_1byte_4_d0_2), .D1_2(rom_1byte_4_d1_2), .D2_2(rom_1byte_4_d2_2),
    .D3_2(rom_1byte_4_d3_2), .D4_2(rom_1byte_4_d4_2), .D5_2(rom_1byte_4_d5_2), .D6_2(rom_1byte_4_d6_2),
    .D7_2(rom_1byte_4_d7_2), .D0(1'b0), .D1(1'b0), .D2(1'b0), .D3(1'b1), .D4(1'b1), .D5(1'b1), .D6(1'b0),
    .D7(1'b1));
  rom_1byte rom_1byte_5 (
    .E(line_decoder_4_to16_1_o4), .D0_2(rom_1byte_5_d0_2), .D1_2(rom_1byte_5_d1_2), .D2_2(rom_1byte_5_d2_2),
    .D3_2(rom_1byte_5_d3_2), .D4_2(rom_1byte_5_d4_2), .D5_2(rom_1byte_5_d5_2), .D6_2(rom_1byte_5_d6_2),
    .D7_2(rom_1byte_5_d7_2), .D0(1'b0), .D1(1'b0), .D2(1'b0), .D3(1'b1), .D4(1'b1), .D5(1'b1), .D6(1'b0),
    .D7(1'b1));
  rom_1byte rom_1byte_6 (
    .E(line_decoder_4_to16_1_o5), .D0_2(rom_1byte_6_d0_2), .D1_2(rom_1byte_6_d1_2), .D2_2(rom_1byte_6_d2_2),
    .D3_2(rom_1byte_6_d3_2), .D4_2(rom_1byte_6_d4_2), .D5_2(rom_1byte_6_d5_2), .D6_2(rom_1byte_6_d6_2),
    .D7_2(rom_1byte_6_d7_2), .D0(1'b0), .D1(1'b0), .D2(1'b1), .D3(1'b1), .D4(1'b1), .D5(1'b1), .D6(1'b0),
    .D7(1'b1));
  rom_1byte rom_1byte_7 (
    .E(line_decoder_4_to16_1_o6), .D0_2(rom_1byte_7_d0_2), .D1_2(rom_1byte_7_d1_2), .D2_2(rom_1byte_7_d2_2),
    .D3_2(rom_1byte_7_d3_2), .D4_2(rom_1byte_7_d4_2), .D5_2(rom_1byte_7_d5_2), .D6_2(rom_1byte_7_d6_2),
    .D7_2(rom_1byte_7_d7_2), .D0(1'b0), .D1(1'b1), .D2(1'b1), .D3(1'b0), .D4(1'b1), .D5(1'b1), .D6(1'b0),
    .D7(1'b1));
  rom_1byte rom_1byte_8 (
    .E(line_decoder_4_to16_1_o7), .D0_2(rom_1byte_8_d0_2), .D1_2(rom_1byte_8_d1_2), .D2_2(rom_1byte_8_d2_2),
    .D3_2(rom_1byte_8_d3_2), .D4_2(rom_1byte_8_d4_2), .D5_2(rom_1byte_8_d5_2), .D6_2(rom_1byte_8_d6_2),
    .D7_2(rom_1byte_8_d7_2), .D0(1'b1), .D1(1'b1), .D2(1'b0), .D3(1'b0), .D4(1'b1), .D5(1'b1), .D6(1'b0),
    .D7(1'b1));
  rom_1byte rom_1byte_9 (
    .E(line_decoder_4_to16_1_o8), .D0_2(rom_1byte_9_d0_2), .D1_2(rom_1byte_9_d1_2), .D2_2(rom_1byte_9_d2_2),
    .D3_2(rom_1byte_9_d3_2), .D4_2(rom_1byte_9_d4_2), .D5_2(rom_1byte_9_d5_2), .D6_2(rom_1byte_9_d6_2),
    .D7_2(rom_1byte_9_d7_2), .D0(1'b1), .D1(1'b0), .D2(1'b0), .D3(1'b0), .D4(1'b1), .D5(1'b1), .D6(1'b0),
    .D7(1'b1));
  rom_1byte rom_1byte_10 (
    .E(line_decoder_4_to16_1_o9), .D0_2(rom_1byte_10_d0_2), .D1_2(rom_1byte_10_d1_2),
    .D2_2(rom_1byte_10_d2_2), .D3_2(rom_1byte_10_d3_2), .D4_2(rom_1byte_10_d4_2), .D5_2(rom_1byte_10_d5_2),
    .D6_2(rom_1byte_10_d6_2), .D7_2(rom_1byte_10_d7_2), .D0(1'b0), .D1(1'b0), .D2(1'b0), .D3(1'b0),
    .D4(1'b1), .D5(1'b1), .D6(1'b1), .D7(1'b1));
  rom_1byte rom_1byte_11 (
    .E(line_decoder_4_to16_1_o10), .D0_2(rom_1byte_11_d0_2), .D1_2(rom_1byte_11_d1_2),
    .D2_2(rom_1byte_11_d2_2), .D3_2(rom_1byte_11_d3_2), .D4_2(rom_1byte_11_d4_2), .D5_2(rom_1byte_11_d5_2),
    .D6_2(rom_1byte_11_d6_2), .D7_2(rom_1byte_11_d7_2), .D0(1'b1), .D1(1'b1), .D2(1'b1), .D3(1'b1),
    .D4(1'b1), .D5(1'b1), .D6(1'b1), .D7(1'b1));
  rom_1byte rom_1byte_12 (
    .E(line_decoder_4_to16_1_o11), .D0_2(rom_1byte_12_d0_2), .D1_2(rom_1byte_12_d1_2),
    .D2_2(rom_1byte_12_d2_2), .D3_2(rom_1byte_12_d3_2), .D4_2(rom_1byte_12_d4_2), .D5_2(rom_1byte_12_d5_2),
    .D6_2(rom_1byte_12_d6_2), .D7_2(rom_1byte_12_d7_2), .D0(1'b1), .D1(1'b1), .D2(1'b1), .D3(1'b1),
    .D4(1'b1), .D5(1'b1), .D6(1'b1), .D7(1'b1));
  rom_1byte rom_1byte_13 (
    .E(line_decoder_4_to16_1_o12), .D0_2(rom_1byte_13_d0_2), .D1_2(rom_1byte_13_d1_2),
    .D2_2(rom_1byte_13_d2_2), .D3_2(rom_1byte_13_d3_2), .D4_2(rom_1byte_13_d4_2), .D5_2(rom_1byte_13_d5_2),
    .D6_2(rom_1byte_13_d6_2), .D7_2(rom_1byte_13_d7_2), .D0(1'b1), .D1(1'b1), .D2(1'b1), .D3(1'b1),
    .D4(1'b1), .D5(1'b1), .D6(1'b1), .D7(1'b1));
  rom_1byte rom_1byte_14 (
    .E(line_decoder_4_to16_1_o13), .D0_2(rom_1byte_14_d0_2), .D1_2(rom_1byte_14_d1_2),
    .D2_2(rom_1byte_14_d2_2), .D3_2(rom_1byte_14_d3_2), .D4_2(rom_1byte_14_d4_2), .D5_2(rom_1byte_14_d5_2),
    .D6_2(rom_1byte_14_d6_2), .D7_2(rom_1byte_14_d7_2), .D0(1'b1), .D1(1'b1), .D2(1'b1), .D3(1'b1),
    .D4(1'b1), .D5(1'b1), .D6(1'b1), .D7(1'b1));
  rom_1byte rom_1byte_15 (
    .E(line_decoder_4_to16_1_o14), .D0_2(rom_1byte_15_d0_2), .D1_2(rom_1byte_15_d1_2),
    .D2_2(rom_1byte_15_d2_2), .D3_2(rom_1byte_15_d3_2), .D4_2(rom_1byte_15_d4_2), .D5_2(rom_1byte_15_d5_2),
    .D6_2(rom_1byte_15_d6_2), .D7_2(rom_1byte_15_d7_2), .D0(1'b1), .D1(1'b1), .D2(1'b1), .D3(1'b1),
    .D4(1'b1), .D5(1'b1), .D6(1'b1), .D7(1'b1));
  rom_1byte rom_1byte_16 (
    .E(line_decoder_4_to16_1_o15), .D0_2(rom_1byte_16_d0_2), .D1_2(rom_1byte_16_d1_2),
    .D2_2(rom_1byte_16_d2_2), .D3_2(rom_1byte_16_d3_2), .D4_2(rom_1byte_16_d4_2), .D5_2(rom_1byte_16_d5_2),
    .D6_2(rom_1byte_16_d6_2), .D7_2(rom_1byte_16_d7_2), .D0(1'b1), .D1(1'b1), .D2(1'b1), .D3(1'b1),
    .D4(1'b1), .D5(1'b1), .D6(1'b1), .D7(1'b1));
  or or_1 (D0, rom_1byte_1_d0_2, rom_1byte_2_d0_2, rom_1byte_3_d0_2, rom_1byte_4_d0_2, rom_1byte_5_d0_2, rom_1byte_6_d0_2, rom_1byte_7_d0_2, rom_1byte_8_d0_2, rom_1byte_9_d0_2, rom_1byte_10_d0_2, rom_1byte_11_d0_2, rom_1byte_12_d0_2, rom_1byte_13_d0_2, rom_1byte_14_d0_2, rom_1byte_15_d0_2, rom_1byte_16_d0_2);
  or or_2 (D1, rom_1byte_1_d1_2, rom_1byte_2_d1_2, rom_1byte_3_d1_2, rom_1byte_4_d1_2, rom_1byte_5_d1_2, rom_1byte_6_d1_2, rom_1byte_7_d1_2, rom_1byte_8_d1_2, rom_1byte_9_d1_2, rom_1byte_10_d1_2, rom_1byte_11_d1_2, rom_1byte_12_d1_2, rom_1byte_13_d1_2, rom_1byte_14_d1_2, rom_1byte_15_d1_2, rom_1byte_16_d1_2);
  or or_3 (D2, rom_1byte_1_d2_2, rom_1byte_2_d2_2, rom_1byte_3_d2_2, rom_1byte_4_d2_2, rom_1byte_5_d2_2, rom_1byte_6_d2_2, rom_1byte_7_d2_2, rom_1byte_8_d2_2, rom_1byte_9_d2_2, rom_1byte_10_d2_2, rom_1byte_11_d2_2, rom_1byte_12_d2_2, rom_1byte_13_d2_2, rom_1byte_14_d2_2, rom_1byte_15_d2_2, rom_1byte_16_d2_2);
  or or_4 (D3, rom_1byte_1_d3_2, rom_1byte_2_d3_2, rom_1byte_3_d3_2, rom_1byte_4_d3_2, rom_1byte_5_d3_2, rom_1byte_6_d3_2, rom_1byte_7_d3_2, rom_1byte_8_d3_2, rom_1byte_9_d3_2, rom_1byte_10_d3_2, rom_1byte_11_d3_2, rom_1byte_12_d3_2, rom_1byte_13_d3_2, rom_1byte_14_d3_2, rom_1byte_15_d3_2, rom_1byte_16_d3_2);
  or or_5 (D4, rom_1byte_1_d4_2, rom_1byte_2_d4_2, rom_1byte_3_d4_2, rom_1byte_4_d4_2, rom_1byte_5_d4_2, rom_1byte_6_d4_2, rom_1byte_7_d4_2, rom_1byte_8_d4_2, rom_1byte_9_d4_2, rom_1byte_10_d4_2, rom_1byte_11_d4_2, rom_1byte_12_d4_2, rom_1byte_13_d4_2, rom_1byte_14_d4_2, rom_1byte_15_d4_2, rom_1byte_16_d4_2);
  or or_6 (D5, rom_1byte_1_d5_2, rom_1byte_2_d5_2, rom_1byte_3_d5_2, rom_1byte_4_d5_2, rom_1byte_5_d5_2, rom_1byte_6_d5_2, rom_1byte_7_d5_2, rom_1byte_8_d5_2, rom_1byte_9_d5_2, rom_1byte_10_d5_2, rom_1byte_11_d5_2, rom_1byte_12_d5_2, rom_1byte_13_d5_2, rom_1byte_14_d5_2, rom_1byte_15_d5_2, rom_1byte_16_d5_2);
  or or_7 (D6, rom_1byte_1_d6_2, rom_1byte_2_d6_2, rom_1byte_3_d6_2, rom_1byte_4_d6_2, rom_1byte_5_d6_2, rom_1byte_6_d6_2, rom_1byte_7_d6_2, rom_1byte_8_d6_2, rom_1byte_9_d6_2, rom_1byte_10_d6_2, rom_1byte_11_d6_2, rom_1byte_12_d6_2, rom_1byte_13_d6_2, rom_1byte_14_d6_2, rom_1byte_15_d6_2, rom_1byte_16_d6_2);
  or or_8 (D7, rom_1byte_1_d7_2, rom_1byte_2_d7_2, rom_1byte_3_d7_2, rom_1byte_4_d7_2, rom_1byte_5_d7_2, rom_1byte_6_d7_2, rom_1byte_7_d7_2, rom_1byte_8_d7_2, rom_1byte_9_d7_2, rom_1byte_10_d7_2, rom_1byte_11_d7_2, rom_1byte_12_d7_2, rom_1byte_13_d7_2, rom_1byte_14_d7_2, rom_1byte_15_d7_2, rom_1byte_16_d7_2);
endmodule

module rom_Timer (
  input  A0,
  input  A1,
  input  A2,
  input  A3,
  output D0,
  output D1,
  output D2,
  output D3,
  output D4,
  output D5,
  output D6,
  output D7
);

  wire line_decoder_4_to16_1_o0, line_decoder_4_to16_1_o1, line_decoder_4_to16_1_o2,
       line_decoder_4_to16_1_o3, line_decoder_4_to16_1_o4, line_decoder_4_to16_1_o5,
       line_decoder_4_to16_1_o6, line_decoder_4_to16_1_o7, line_decoder_4_to16_1_o8,
       line_decoder_4_to16_1_o9, line_decoder_4_to16_1_o10, line_decoder_4_to16_1_o11,
       line_decoder_4_to16_1_o12, line_decoder_4_to16_1_o13, line_decoder_4_to16_1_o14,
       line_decoder_4_to16_1_o15, rom_1byte_1_d0_2, rom_1byte_1_d1_2, rom_1byte_1_d2_2, rom_1byte_1_d3_2,
       rom_1byte_1_d4_2, rom_1byte_1_d5_2, rom_1byte_1_d6_2, rom_1byte_1_d7_2, rom_1byte_2_d0_2,
       rom_1byte_2_d1_2, rom_1byte_2_d2_2, rom_1byte_2_d3_2, rom_1byte_2_d4_2, rom_1byte_2_d5_2,
       rom_1byte_2_d6_2, rom_1byte_2_d7_2, rom_1byte_3_d0_2, rom_1byte_3_d1_2, rom_1byte_3_d2_2,
       rom_1byte_3_d3_2, rom_1byte_3_d4_2, rom_1byte_3_d5_2, rom_1byte_3_d6_2, rom_1byte_3_d7_2,
       rom_1byte_4_d0_2, rom_1byte_4_d1_2, rom_1byte_4_d2_2, rom_1byte_4_d3_2, rom_1byte_4_d4_2,
       rom_1byte_4_d5_2, rom_1byte_4_d6_2, rom_1byte_4_d7_2, rom_1byte_5_d0_2, rom_1byte_5_d1_2,
       rom_1byte_5_d2_2, rom_1byte_5_d3_2, rom_1byte_5_d4_2, rom_1byte_5_d5_2, rom_1byte_5_d6_2,
       rom_1byte_5_d7_2, rom_1byte_6_d0_2, rom_1byte_6_d1_2, rom_1byte_6_d2_2, rom_1byte_6_d3_2,
       rom_1byte_6_d4_2, rom_1byte_6_d5_2, rom_1byte_6_d6_2, rom_1byte_6_d7_2, rom_1byte_7_d0_2,
       rom_1byte_7_d1_2, rom_1byte_7_d2_2, rom_1byte_7_d3_2, rom_1byte_7_d4_2, rom_1byte_7_d5_2,
       rom_1byte_7_d6_2, rom_1byte_7_d7_2, rom_1byte_8_d0_2, rom_1byte_8_d1_2, rom_1byte_8_d2_2,
       rom_1byte_8_d3_2, rom_1byte_8_d4_2, rom_1byte_8_d5_2, rom_1byte_8_d6_2, rom_1byte_8_d7_2,
       rom_1byte_9_d0_2, rom_1byte_9_d1_2, rom_1byte_9_d2_2, rom_1byte_9_d3_2, rom_1byte_9_d4_2,
       rom_1byte_9_d5_2, rom_1byte_9_d6_2, rom_1byte_9_d7_2, rom_1byte_10_d0_2, rom_1byte_10_d1_2,
       rom_1byte_10_d2_2, rom_1byte_10_d3_2, rom_1byte_10_d4_2, rom_1byte_10_d5_2, rom_1byte_10_d6_2,
       rom_1byte_10_d7_2, rom_1byte_11_d0_2, rom_1byte_11_d1_2, rom_1byte_11_d2_2, rom_1byte_11_d3_2,
       rom_1byte_11_d4_2, rom_1byte_11_d5_2, rom_1byte_11_d6_2, rom_1byte_11_d7_2, rom_1byte_12_d0_2,
       rom_1byte_12_d1_2, rom_1byte_12_d2_2, rom_1byte_12_d3_2, rom_1byte_12_d4_2, rom_1byte_12_d5_2,
       rom_1byte_12_d6_2, rom_1byte_12_d7_2, rom_1byte_13_d0_2, rom_1byte_13_d1_2, rom_1byte_13_d2_2,
       rom_1byte_13_d3_2, rom_1byte_13_d4_2, rom_1byte_13_d5_2, rom_1byte_13_d6_2, rom_1byte_13_d7_2,
       rom_1byte_14_d0_2, rom_1byte_14_d1_2, rom_1byte_14_d2_2, rom_1byte_14_d3_2, rom_1byte_14_d4_2,
       rom_1byte_14_d5_2, rom_1byte_14_d6_2, rom_1byte_14_d7_2, rom_1byte_15_d0_2, rom_1byte_15_d1_2,
       rom_1byte_15_d2_2, rom_1byte_15_d3_2, rom_1byte_15_d4_2, rom_1byte_15_d5_2, rom_1byte_15_d6_2,
       rom_1byte_15_d7_2, rom_1byte_16_d0_2, rom_1byte_16_d1_2, rom_1byte_16_d2_2, rom_1byte_16_d3_2,
       rom_1byte_16_d4_2, rom_1byte_16_d5_2, rom_1byte_16_d6_2, rom_1byte_16_d7_2;

  line_decoder_4_to16 line_decoder_4_to16_1 (
    .S0(A0), .S1(A1), .S3(A2), .S4(A3), .In(1'b1), .O15(line_decoder_4_to16_1_o15),
    .O14(line_decoder_4_to16_1_o14), .O13(line_decoder_4_to16_1_o13), .O12(line_decoder_4_to16_1_o12),
    .O11(line_decoder_4_to16_1_o11), .O10(line_decoder_4_to16_1_o10), .O9(line_decoder_4_to16_1_o9),
    .O8(line_decoder_4_to16_1_o8), .O7(line_decoder_4_to16_1_o7), .O6(line_decoder_4_to16_1_o6),
    .O5(line_decoder_4_to16_1_o5), .O4(line_decoder_4_to16_1_o4), .O3(line_decoder_4_to16_1_o3),
    .O2(line_decoder_4_to16_1_o2), .O1(line_decoder_4_to16_1_o1), .O0(line_decoder_4_to16_1_o0));
  rom_1byte rom_1byte_1 (
    .E(line_decoder_4_to16_1_o0), .D0_2(rom_1byte_1_d0_2), .D1_2(rom_1byte_1_d1_2), .D2_2(rom_1byte_1_d2_2),
    .D3_2(rom_1byte_1_d3_2), .D4_2(rom_1byte_1_d4_2), .D5_2(rom_1byte_1_d5_2), .D6_2(rom_1byte_1_d6_2),
    .D7_2(rom_1byte_1_d7_2), .D0(1'b1), .D1(1'b1), .D2(1'b1), .D3(1'b0), .D4(1'b1), .D5(1'b1), .D6(1'b0),
    .D7(1'b1));
  rom_1byte rom_1byte_2 (
    .E(line_decoder_4_to16_1_o1), .D0_2(rom_1byte_2_d0_2), .D1_2(rom_1byte_2_d1_2), .D2_2(rom_1byte_2_d2_2),
    .D3_2(rom_1byte_2_d3_2), .D4_2(rom_1byte_2_d4_2), .D5_2(rom_1byte_2_d5_2), .D6_2(rom_1byte_2_d6_2),
    .D7_2(rom_1byte_2_d7_2), .D0(1'b1), .D1(1'b0), .D2(1'b0), .D3(1'b0), .D4(1'b0), .D5(1'b0), .D6(1'b0),
    .D7(1'b0));
  rom_1byte rom_1byte_3 (
    .E(line_decoder_4_to16_1_o2), .D0_2(rom_1byte_3_d0_2), .D1_2(rom_1byte_3_d1_2), .D2_2(rom_1byte_3_d2_2),
    .D3_2(rom_1byte_3_d3_2), .D4_2(rom_1byte_3_d4_2), .D5_2(rom_1byte_3_d5_2), .D6_2(rom_1byte_3_d6_2),
    .D7_2(rom_1byte_3_d7_2), .D0(1'b1), .D1(1'b0), .D2(1'b0), .D3(1'b0), .D4(1'b0), .D5(1'b1), .D6(1'b1),
    .D7(1'b1));
  rom_1byte rom_1byte_4 (
    .E(line_decoder_4_to16_1_o3), .D0_2(rom_1byte_4_d0_2), .D1_2(rom_1byte_4_d1_2), .D2_2(rom_1byte_4_d2_2),
    .D3_2(rom_1byte_4_d3_2), .D4_2(rom_1byte_4_d4_2), .D5_2(rom_1byte_4_d5_2), .D6_2(rom_1byte_4_d6_2),
    .D7_2(rom_1byte_4_d7_2), .D0(1'b1), .D1(1'b0), .D2(1'b0), .D3(1'b0), .D4(1'b0), .D5(1'b0), .D6(1'b0),
    .D7(1'b0));
  rom_1byte rom_1byte_5 (
    .E(line_decoder_4_to16_1_o4), .D0_2(rom_1byte_5_d0_2), .D1_2(rom_1byte_5_d1_2), .D2_2(rom_1byte_5_d2_2),
    .D3_2(rom_1byte_5_d3_2), .D4_2(rom_1byte_5_d4_2), .D5_2(rom_1byte_5_d5_2), .D6_2(rom_1byte_5_d6_2),
    .D7_2(rom_1byte_5_d7_2), .D0(1'b1), .D1(1'b1), .D2(1'b0), .D3(1'b0), .D4(1'b0), .D5(1'b0), .D6(1'b0),
    .D7(1'b0));
  rom_1byte rom_1byte_6 (
    .E(line_decoder_4_to16_1_o5), .D0_2(rom_1byte_6_d0_2), .D1_2(rom_1byte_6_d1_2), .D2_2(rom_1byte_6_d2_2),
    .D3_2(rom_1byte_6_d3_2), .D4_2(rom_1byte_6_d4_2), .D5_2(rom_1byte_6_d5_2), .D6_2(rom_1byte_6_d6_2),
    .D7_2(rom_1byte_6_d7_2), .D0(1'b0), .D1(1'b1), .D2(1'b1), .D3(1'b0), .D4(1'b1), .D5(1'b1), .D6(1'b0),
    .D7(1'b1));
  rom_1byte rom_1byte_7 (
    .E(line_decoder_4_to16_1_o6), .D0_2(rom_1byte_7_d0_2), .D1_2(rom_1byte_7_d1_2), .D2_2(rom_1byte_7_d2_2),
    .D3_2(rom_1byte_7_d3_2), .D4_2(rom_1byte_7_d4_2), .D5_2(rom_1byte_7_d5_2), .D6_2(rom_1byte_7_d6_2),
    .D7_2(rom_1byte_7_d7_2), .D0(1'b1), .D1(1'b0), .D2(1'b0), .D3(1'b0), .D4(1'b0), .D5(1'b0), .D6(1'b0),
    .D7(1'b0));
  rom_1byte rom_1byte_8 (
    .E(line_decoder_4_to16_1_o7), .D0_2(rom_1byte_8_d0_2), .D1_2(rom_1byte_8_d1_2), .D2_2(rom_1byte_8_d2_2),
    .D3_2(rom_1byte_8_d3_2), .D4_2(rom_1byte_8_d4_2), .D5_2(rom_1byte_8_d5_2), .D6_2(rom_1byte_8_d6_2),
    .D7_2(rom_1byte_8_d7_2), .D0(1'b0), .D1(1'b1), .D2(1'b1), .D3(1'b0), .D4(1'b0), .D5(1'b1), .D6(1'b1),
    .D7(1'b1));
  rom_1byte rom_1byte_9 (
    .E(line_decoder_4_to16_1_o8), .D0_2(rom_1byte_9_d0_2), .D1_2(rom_1byte_9_d1_2), .D2_2(rom_1byte_9_d2_2),
    .D3_2(rom_1byte_9_d3_2), .D4_2(rom_1byte_9_d4_2), .D5_2(rom_1byte_9_d5_2), .D6_2(rom_1byte_9_d6_2),
    .D7_2(rom_1byte_9_d7_2), .D0(1'b1), .D1(1'b0), .D2(1'b0), .D3(1'b0), .D4(1'b0), .D5(1'b0), .D6(1'b0),
    .D7(1'b0));
  rom_1byte rom_1byte_10 (
    .E(line_decoder_4_to16_1_o9), .D0_2(rom_1byte_10_d0_2), .D1_2(rom_1byte_10_d1_2),
    .D2_2(rom_1byte_10_d2_2), .D3_2(rom_1byte_10_d3_2), .D4_2(rom_1byte_10_d4_2), .D5_2(rom_1byte_10_d5_2),
    .D6_2(rom_1byte_10_d6_2), .D7_2(rom_1byte_10_d7_2), .D0(1'b0), .D1(1'b0), .D2(1'b0), .D3(1'b1),
    .D4(1'b0), .D5(1'b1), .D6(1'b1), .D7(1'b1));
  rom_1byte rom_1byte_11 (
    .E(line_decoder_4_to16_1_o10), .D0_2(rom_1byte_11_d0_2), .D1_2(rom_1byte_11_d1_2),
    .D2_2(rom_1byte_11_d2_2), .D3_2(rom_1byte_11_d3_2), .D4_2(rom_1byte_11_d4_2), .D5_2(rom_1byte_11_d5_2),
    .D6_2(rom_1byte_11_d6_2), .D7_2(rom_1byte_11_d7_2), .D0(1'b0), .D1(1'b0), .D2(1'b0), .D3(1'b0),
    .D4(1'b1), .D5(1'b1), .D6(1'b0), .D7(1'b1));
  rom_1byte rom_1byte_12 (
    .E(line_decoder_4_to16_1_o11), .D0_2(rom_1byte_12_d0_2), .D1_2(rom_1byte_12_d1_2),
    .D2_2(rom_1byte_12_d2_2), .D3_2(rom_1byte_12_d3_2), .D4_2(rom_1byte_12_d4_2), .D5_2(rom_1byte_12_d5_2),
    .D6_2(rom_1byte_12_d6_2), .D7_2(rom_1byte_12_d7_2), .D0(1'b0), .D1(1'b0), .D2(1'b1), .D3(1'b0),
    .D4(1'b1), .D5(1'b1), .D6(1'b0), .D7(1'b1));
  rom_1byte rom_1byte_13 (
    .E(line_decoder_4_to16_1_o12), .D0_2(rom_1byte_13_d0_2), .D1_2(rom_1byte_13_d1_2),
    .D2_2(rom_1byte_13_d2_2), .D3_2(rom_1byte_13_d3_2), .D4_2(rom_1byte_13_d4_2), .D5_2(rom_1byte_13_d5_2),
    .D6_2(rom_1byte_13_d6_2), .D7_2(rom_1byte_13_d7_2), .D0(1'b1), .D1(1'b0), .D2(1'b0), .D3(1'b0),
    .D4(1'b0), .D5(1'b0), .D6(1'b0), .D7(1'b0));
  rom_1byte rom_1byte_14 (
    .E(line_decoder_4_to16_1_o13), .D0_2(rom_1byte_14_d0_2), .D1_2(rom_1byte_14_d1_2),
    .D2_2(rom_1byte_14_d2_2), .D3_2(rom_1byte_14_d3_2), .D4_2(rom_1byte_14_d4_2), .D5_2(rom_1byte_14_d5_2),
    .D6_2(rom_1byte_14_d6_2), .D7_2(rom_1byte_14_d7_2), .D0(1'b0), .D1(1'b1), .D2(1'b0), .D3(1'b1),
    .D4(1'b0), .D5(1'b1), .D6(1'b1), .D7(1'b1));
  rom_1byte rom_1byte_15 (
    .E(line_decoder_4_to16_1_o14), .D0_2(rom_1byte_15_d0_2), .D1_2(rom_1byte_15_d1_2),
    .D2_2(rom_1byte_15_d2_2), .D3_2(rom_1byte_15_d3_2), .D4_2(rom_1byte_15_d4_2), .D5_2(rom_1byte_15_d5_2),
    .D6_2(rom_1byte_15_d6_2), .D7_2(rom_1byte_15_d7_2), .D0(1'b0), .D1(1'b0), .D2(1'b0), .D3(1'b1),
    .D4(1'b1), .D5(1'b1), .D6(1'b0), .D7(1'b1));
  rom_1byte rom_1byte_16 (
    .E(line_decoder_4_to16_1_o15), .D0_2(rom_1byte_16_d0_2), .D1_2(rom_1byte_16_d1_2),
    .D2_2(rom_1byte_16_d2_2), .D3_2(rom_1byte_16_d3_2), .D4_2(rom_1byte_16_d4_2), .D5_2(rom_1byte_16_d5_2),
    .D6_2(rom_1byte_16_d6_2), .D7_2(rom_1byte_16_d7_2), .D0(1'b1), .D1(1'b1), .D2(1'b1), .D3(1'b1),
    .D4(1'b1), .D5(1'b1), .D6(1'b1), .D7(1'b1));
  or or_1 (D0, rom_1byte_1_d0_2, rom_1byte_2_d0_2, rom_1byte_3_d0_2, rom_1byte_4_d0_2, rom_1byte_5_d0_2, rom_1byte_6_d0_2, rom_1byte_7_d0_2, rom_1byte_8_d0_2, rom_1byte_9_d0_2, rom_1byte_10_d0_2, rom_1byte_11_d0_2, rom_1byte_12_d0_2, rom_1byte_13_d0_2, rom_1byte_14_d0_2, rom_1byte_15_d0_2, rom_1byte_16_d0_2);
  or or_2 (D1, rom_1byte_1_d1_2, rom_1byte_2_d1_2, rom_1byte_3_d1_2, rom_1byte_4_d1_2, rom_1byte_5_d1_2, rom_1byte_6_d1_2, rom_1byte_7_d1_2, rom_1byte_8_d1_2, rom_1byte_9_d1_2, rom_1byte_10_d1_2, rom_1byte_11_d1_2, rom_1byte_12_d1_2, rom_1byte_13_d1_2, rom_1byte_14_d1_2, rom_1byte_15_d1_2, rom_1byte_16_d1_2);
  or or_3 (D2, rom_1byte_1_d2_2, rom_1byte_2_d2_2, rom_1byte_3_d2_2, rom_1byte_4_d2_2, rom_1byte_5_d2_2, rom_1byte_6_d2_2, rom_1byte_7_d2_2, rom_1byte_8_d2_2, rom_1byte_9_d2_2, rom_1byte_10_d2_2, rom_1byte_11_d2_2, rom_1byte_12_d2_2, rom_1byte_13_d2_2, rom_1byte_14_d2_2, rom_1byte_15_d2_2, rom_1byte_16_d2_2);
  or or_4 (D3, rom_1byte_1_d3_2, rom_1byte_2_d3_2, rom_1byte_3_d3_2, rom_1byte_4_d3_2, rom_1byte_5_d3_2, rom_1byte_6_d3_2, rom_1byte_7_d3_2, rom_1byte_8_d3_2, rom_1byte_9_d3_2, rom_1byte_10_d3_2, rom_1byte_11_d3_2, rom_1byte_12_d3_2, rom_1byte_13_d3_2, rom_1byte_14_d3_2, rom_1byte_15_d3_2, rom_1byte_16_d3_2);
  or or_5 (D4, rom_1byte_1_d4_2, rom_1byte_2_d4_2, rom_1byte_3_d4_2, rom_1byte_4_d4_2, rom_1byte_5_d4_2, rom_1byte_6_d4_2, rom_1byte_7_d4_2, rom_1byte_8_d4_2, rom_1byte_9_d4_2, rom_1byte_10_d4_2, rom_1byte_11_d4_2, rom_1byte_12_d4_2, rom_1byte_13_d4_2, rom_1byte_14_d4_2, rom_1byte_15_d4_2, rom_1byte_16_d4_2);
  or or_6 (D5, rom_1byte_1_d5_2, rom_1byte_2_d5_2, rom_1byte_3_d5_2, rom_1byte_4_d5_2, rom_1byte_5_d5_2, rom_1byte_6_d5_2, rom_1byte_7_d5_2, rom_1byte_8_d5_2, rom_1byte_9_d5_2, rom_1byte_10_d5_2, rom_1byte_11_d5_2, rom_1byte_12_d5_2, rom_1byte_13_d5_2, rom_1byte_14_d5_2, rom_1byte_15_d5_2, rom_1byte_16_d5_2);
  or or_7 (D6, rom_1byte_1_d6_2, rom_1byte_2_d6_2, rom_1byte_3_d6_2, rom_1byte_4_d6_2, rom_1byte_5_d6_2, rom_1byte_6_d6_2, rom_1byte_7_d6_2, rom_1byte_8_d6_2, rom_1byte_9_d6_2, rom_1byte_10_d6_2, rom_1byte_11_d6_2, rom_1byte_12_d6_2, rom_1byte_13_d6_2, rom_1byte_14_d6_2, rom_1byte_15_d6_2, rom_1byte_16_d6_2);
  or or_8 (D7, rom_1byte_1_d7_2, rom_1byte_2_d7_2, rom_1byte_3_d7_2, rom_1byte_4_d7_2, rom_1byte_5_d7_2, rom_1byte_6_d7_2, rom_1byte_7_d7_2, rom_1byte_8_d7_2, rom_1byte_9_d7_2, rom_1byte_10_d7_2, rom_1byte_11_d7_2, rom_1byte_12_d7_2, rom_1byte_13_d7_2, rom_1byte_14_d7_2, rom_1byte_15_d7_2, rom_1byte_16_d7_2);
endmodule

// mp4_2
module multiplexer_4_2 (
  input  _0A0,
  input  _0A1,
  input  _0A2,
  input  _0A3,
  input  _1A0,
  input  _1A1,
  input  _1A2,
  input  _1A3,
  input  S1,
  input  S0,
  output _0Y,
  output _1Y
);

  wire and_1_out, and_2_out, and_3_out, and_4_out, and_5_out, and_6_out, and_7_out, and_8_out, not_1_out,
       not_2_out;

  not not_1 (not_1_out, S0);
  not not_2 (not_2_out, S1);
  and and_1 (and_1_out, not_2_out, not_1_out, _0A0);
  and and_2 (and_2_out, not_2_out, S0, _0A1);
  and and_3 (and_3_out, S1, not_1_out, _0A2);
  and and_4 (and_4_out, S1, S0, _0A3);
  and and_5 (and_5_out, not_2_out, not_1_out, _1A0);
  and and_6 (and_6_out, not_2_out, S0, _1A1);
  and and_7 (and_7_out, S1, not_1_out, _1A2);
  and and_8 (and_8_out, S1, S0, _1A3);
  or or_1 (_0Y, and_1_out, and_2_out, and_3_out, and_4_out);
  or or_2 (_1Y, and_5_out, and_6_out, and_7_out, and_8_out);
endmodule

module reg_4 (
  input  D0,
  input  D1,
  input  D2,
  input  D3,
  input  L,
  input  CK,
  input  R1,
  input  R0,
  output Q0,
  output Q1,
  output Q2,
  output Q3
);

  wire d_ff_1_q, d_ff_2_q, d_ff_3_q, d_ff_4_q, multiplexer_2_1_y, multiplexer_2_2_y, multiplexer_2_3_y,
       multiplexer_2_4_y, not_1_out, or_1_out, or_2_out, or_3_out, or_4_out;

  multiplexer_2 multiplexer_2_1 (.A1(Q0), .A2(D0), .S(L), .Y(multiplexer_2_1_y));
  multiplexer_2 multiplexer_2_2 (.A1(Q1), .A2(D1), .S(L), .Y(multiplexer_2_2_y));
  multiplexer_2 multiplexer_2_3 (.A1(Q2), .A2(D2), .S(L), .Y(multiplexer_2_3_y));
  multiplexer_2 multiplexer_2_4 (.A1(Q3), .A2(D3), .S(L), .Y(multiplexer_2_4_y));
  D_Flip_Flop d_ff_1 (.clk(CK), .D(multiplexer_2_1_y), .Q(d_ff_1_q));  // open: Qn, preset, en, reset
  or or_1 (or_1_out, d_ff_1_q, R1);
  D_Flip_Flop d_ff_2 (.clk(CK), .D(multiplexer_2_2_y), .Q(d_ff_2_q));  // open: Qn, preset, en, reset
  or or_2 (or_2_out, d_ff_2_q, R1);
  D_Flip_Flop d_ff_3 (.clk(CK), .D(multiplexer_2_3_y), .Q(d_ff_3_q));  // open: Qn, preset, en, reset
  or or_3 (or_3_out, d_ff_3_q, R1);
  D_Flip_Flop d_ff_4 (.clk(CK), .D(multiplexer_2_4_y), .Q(d_ff_4_q));  // open: Qn, preset, en, reset
  or or_4 (or_4_out, d_ff_4_q, R1);
  not not_1 (not_1_out, R0);
  and and_1 (Q0, or_1_out, not_1_out);
  and and_2 (Q1, or_2_out, not_1_out);
  and and_3 (Q2, or_3_out, not_1_out);
  and and_4 (Q3, or_4_out, not_1_out);
endmodule

// mp_2
module multiplexer_2 (
  input  A1,
  input  A2,
  input  S,
  output Y
);

  wire and_1_out, and_2_out, not_1_out;

  not not_1 (not_1_out, S);
  and and_1 (and_1_out, not_1_out, A1);
  and and_2 (and_2_out, S, A2);
  or or_1 (Y, and_1_out, and_2_out);
endmodule

module _4bit_7seg (
  input  A0,
  input  A1,
  input  A2,
  input  A3,
  output Y0,
  output Y1,
  output Y2,
  output Y3,
  output Y4,
  output Y5,
  output Y6,
  output Y7
);

  _7_Segment_Display u_7_segment_display_1 ();  // open: g, f, a, b, e, d, c, dp
endmodule

module HA (
  input  A,
  input  B,
  output S,
  output C
);

  wire not_1_out, or_1_out;

  or or_1 (or_1_out, A, B);
  not not_1 (not_1_out, C);
  and and_1 (C, A, B);
  and and_2 (S, or_1_out, not_1_out);
endmodule

module FA (
  input  Ci,
  input  A,
  input  B,
  output S,
  output Co
);

  wire ha_1_c, ha_1_s, ha_2_c;

  HA ha_1 (.A(A), .B(B), .S(ha_1_s), .C(ha_1_c));
  HA ha_2 (.A(Ci), .B(ha_1_s), .S(S), .C(ha_2_c));
  or or_1 (Co, ha_2_c, ha_1_c);
endmodule

module FA_4 (
  input  Ci,
  input  A0,
  input  B0,
  input  A1,
  input  B1,
  input  A2,
  input  B2,
  input  A3,
  input  B3,
  output S0,
  output S1,
  output S2,
  output S3,
  output Co
);

  wire fa_1_co, fa_2_co, fa_3_co;

  FA fa_1 (.Ci(Ci), .A(A0), .B(B0), .S(S0), .Co(fa_1_co));
  FA fa_2 (.Ci(fa_1_co), .A(A1), .B(B1), .S(S1), .Co(fa_2_co));
  FA fa_3 (.Ci(fa_2_co), .A(A2), .B(B2), .S(S2), .Co(fa_3_co));
  FA fa_4 (.Ci(fa_3_co), .A(A3), .B(B3), .S(S3), .Co(Co));
endmodule

module count_4 (
  input  D0,
  input  D1,
  input  D2,
  input  D3,
  input  L,
  input  CK,
  input  RST,
  output Q3,
  output Q2,
  output Q1,
  output Q0
);

  wire fa_4_1_s0, fa_4_1_s1, fa_4_1_s2, fa_4_1_s3, multiplexer_4_2_1__0y, multiplexer_4_2_1__1y,
       multiplexer_4_2_2__0y, multiplexer_4_2_2__1y, not_1_out;

  multiplexer_4_2 multiplexer_4_2_1 (
    ._0A0(fa_4_1_s0), ._0A1(D0), .S1(1'b0), .S0(L), ._0Y(multiplexer_4_2_1__0y), ._1Y(multiplexer_4_2_1__1y),
    ._1A0(fa_4_1_s1), ._1A1(D1));  // open: _0A2, _0A3, _1A2, _1A3
  multiplexer_4_2 multiplexer_4_2_2 (
    ._0A0(fa_4_1_s2), ._0A1(D2), .S1(1'b0), .S0(L), ._0Y(multiplexer_4_2_2__0y), ._1Y(multiplexer_4_2_2__1y),
    ._1A0(fa_4_1_s3), ._1A1(D3));  // open: _0A2, _0A3, _1A2, _1A3
  not not_1 (not_1_out, RST);
  reg_4 reg_4_1 (
    .D0(multiplexer_4_2_1__0y), .D1(multiplexer_4_2_1__1y), .D2(multiplexer_4_2_2__0y),
    .D3(multiplexer_4_2_2__1y), .Q0(Q0), .Q1(Q1), .Q2(Q2), .Q3(Q3), .L(not_1_out), .CK(CK), .R0(RST));  // open: R1
  LED led_1 (.in(Q2));
  LED led_2 (.in(Q1));
  LED led_3 (.in(Q3));
  LED led_4 (.in(Q0));
  FA_4 fa_4_1 (
    .A0(Q0), .B0(1'b1), .A1(Q1), .B1(1'b0), .A2(Q2), .B2(1'b0), .A3(Q3), .B3(1'b0), .S0(fa_4_1_s0),
    .S1(fa_4_1_s1), .S2(fa_4_1_s2), .S3(fa_4_1_s3));  // open: Ci, Co
endmodule

module rom_1byte (
  input  E,
  input  D0,
  input  D1,
  input  D2,
  input  D3,
  input  D4,
  input  D5,
  input  D6,
  input  D7,
  output D0_2,
  output D1_2,
  output D2_2,
  output D3_2,
  output D4_2,
  output D5_2,
  output D6_2,
  output D7_2
);

  and and_1 (D0_2, E, D0);
  and and_2 (D1_2, E, D1);
  and and_3 (D2_2, E, D2);
  and and_4 (D3_2, E, D3);
  and and_5 (D4_2, E, D4);
  and and_6 (D5_2, E, D5);
  and and_7 (D6_2, E, D6);
  and and_8 (D7_2, E, D7);
endmodule

// dec_2_4
module line_decoder_2_to_4 (
  input  In,
  input  S0,
  input  S1,
  input  E,
  output O0,
  output O1,
  output O2,
  output O3
);

  wire not_1_out, not_2_out, not_3_out;

  not not_1 (not_1_out, S0);
  not not_2 (not_2_out, S1);
  not not_3 (not_3_out, E);
  and and_1 (O0, not_1_out, not_2_out, In, not_3_out);
  and and_2 (O1, S0, not_2_out, In, not_3_out);
  and and_3 (O2, not_1_out, S1, In, not_3_out);
  and and_4 (O3, S0, S1, In, not_3_out);
endmodule

// dec_2_4
module line_decoder_4_to16 (
  input  S0,
  input  S1,
  input  S3,
  input  S4,
  input  In,
  output O15,
  output O14,
  output O13,
  output O12,
  output O11,
  output O10,
  output O9,
  output O8,
  output O7,
  output O6,
  output O5,
  output O4,
  output O3,
  output O2,
  output O1,
  output O0
);

  wire not_1_out, not_2_out, or_1_out, or_2_out, or_3_out, or_4_out;

  not not_1 (not_1_out, S3);
  not not_2 (not_2_out, S4);
  or or_1 (or_1_out, S3, S4);
  or or_2 (or_2_out, not_1_out, S4);
  or or_3 (or_3_out, not_2_out, S3);
  or or_4 (or_4_out, not_2_out, not_1_out);
  line_decoder_2_to_4 line_decoder_2_to_4_1 (
    .In(In), .S0(S0), .S1(S1), .E(or_1_out), .O0(O0), .O1(O1), .O2(O2), .O3(O3));
  line_decoder_2_to_4 line_decoder_2_to_4_2 (
    .In(In), .S0(S0), .S1(S1), .E(or_2_out), .O0(O4), .O1(O5), .O2(O6), .O3(O7));
  line_decoder_2_to_4 line_decoder_2_to_4_3 (
    .In(In), .S0(S0), .S1(S1), .E(or_3_out), .O0(O8), .O1(O9), .O2(O10), .O3(O11));
  line_decoder_2_to_4 line_decoder_2_to_4_4 (
    .In(In), .S0(S0), .S1(S1), .E(or_4_out), .O0(O12), .O1(O13), .O2(O14), .O3(O15));
endmodule

// decoder
module ins_decoder (
  input  D0,
  input  D1,
  input  D2,
  input  D3,
  input  D4,
  input  D5,
  input  D6,
  input  D7,
  input  C,
  output im0,
  output im1,
  output im2,
  output im3,
  output L_A,
  output L_B,
  output L_C,
  output L_D,
  output S0,
  output S1
);

  wire and_1_out, not_1_out, not_2_out, not_3_out, not_4_out, not_5_out, or_1_out, or_2_out, or_3_out,
       or_4_out;

  not not_1 (not_1_out, D4);
  not not_2 (not_2_out, D6);
  not not_3 (not_3_out, D7);
  not not_4 (not_4_out, D6);
  not not_5 (not_5_out, D7);
  and and_1 (and_1_out, not_1_out, C);
  or or_1 (or_1_out, D6, D7);
  not not_6 (L_A, or_1_out);
  or or_2 (or_2_out, not_2_out, D7);
  not not_7 (L_B, or_2_out);
  or or_3 (or_3_out, D6, not_3_out);
  not not_8 (L_C, or_3_out);
  not not_9 (L_D, or_4_out);
  or or_4 (or_4_out, not_4_out, not_5_out, and_1_out);
  or or_5 (S0, D6, D7);

  assign im0 = D0;
  assign im1 = D1;
  assign im2 = D2;
  assign im3 = D3;
  assign S1 = D5;

  // Notes on the sheet:
  //   OP0
  //   OP1
  //   OP2
  //   OP3
endmodule

module test (
  input  in_1,
  input  in_2,
  input  in_3,
  output out_4
);

  wire nand_1_out, nand_2_out, not_1_out;

  not not_1 (not_1_out, in_3);
  nand nand_1 (nand_1_out, in_1, not_1_out);
  nand nand_2 (nand_2_out, in_2, in_3);
  nand nand_3 (out_4, nand_1_out, nand_2_out);
endmodule
