// Logisim project register.circ as structural Verilog: 1 circuit, main circuit main
module main (
  input  in_1,
  input  in_2,
  input  REG_A,
  input  REG_B,
  input  in_5
);

  wire and_1_out, and_2_out, and_3_out, and_4_out, and_5_out, and_6_out, and_7_out, clock_1_out, d_ff_1_q,
       d_ff_2_q, not_1_out, not_2_out, not_3_out, or_1_out, or_2_out, or_3_out;

  not not_1 (not_1_out, REG_A);
  not not_2 (not_2_out, REG_B);
  and and_1 (and_1_out, d_ff_1_q, not_1_out);
  and and_2 (and_2_out, REG_A, and_7_out);
  and and_3 (and_3_out, d_ff_2_q, not_2_out);
  and and_4 (and_4_out, REG_B, and_7_out);
  or or_1 (or_1_out, and_1_out, and_2_out);
  Clock clock_1 (.out(clock_1_out));
  or or_2 (or_2_out, and_3_out, and_4_out);
  LED led_1 (.in(d_ff_1_q));
  D_Flip_Flop d_ff_1 (.clk(clock_1_out), .D(or_1_out), .Q(d_ff_1_q));  // open: Qn, preset, en, reset
  LED led_2 (.in(d_ff_2_q));
  D_Flip_Flop d_ff_2 (.clk(clock_1_out), .D(or_2_out), .Q(d_ff_2_q));  // open: Qn, preset, en, reset
  not not_3 (not_3_out, in_1);
  and and_5 (and_5_out, d_ff_1_q, not_3_out);
  and and_6 (and_6_out, in_1, d_ff_2_q);
  or or_3 (or_3_out, and_5_out, in_2, and_6_out);
  and and_7 (and_7_out, or_3_out, in_5);

  // Notes on the sheet:
  //   LOAD
  //   REG[A}
  //   REG[B}
  //   SELECTOR
  //   RESET(NEG)
endmodule
